# Fritzing sketch protoboard (saved by Fritzing 0.9.3b)
breadboards: 1

parts:
  Componente1 = Bluetooth HC-05 Macho
  Componente2 = Arduino Uno (Rev3)
  R1 = Resistor [tolerance=±5% resistance=680 package=THT]
  R2 = Resistor [tolerance=±5% resistance=470 package=THT]
  GY1 = MPU-6050 Board GY-521 [form="♀ (female)" package=THT]

nets:
  N1: Componente1.TXD, Componente2.D0/RX
  N2: Componente1.RXD, R1.Pin_0, R2.Pin_1
  VCC: Componente1.VCC, Componente2.5V, GY1.pin1
  GND: Componente1.GND, Componente2.GND, R1.Pin_1, GY1.pin2
  N3: Componente2.A4/SDA, GY1.pin4
  N4: Componente2.A5/SCL, GY1.pin3
  N5: Componente2.D1/TX, R2.Pin_0

custom parts:
  MPU-6050 Board GY-521: Acelerometro y Giroscopio MPU-6050 Board GY-521

// code stored in the sketch: acelerometro.ino
//Programa : Teste MPU6050 e LCD 20x4
//Alteracoes e adaptacoes : FILIPEFLOP
//
//Baseado no programa original de JohnChi
 
//Carrega a biblioteca Wire
#include<Wire.h>
//Carrega a biblioteca do LCD
#include <LiquidCrystal.h>
 
// Inicializa o LCD
LiquidCrystal lcd(12, 11, 5, 4, 3, 2);
 
//Endereco I2C do MPU6050
const int MPU=0x68;  
//Variaveis para armazenar valores dos sensores
int AcX,AcY,AcZ,Tmp,GyX,GyY,GyZ;
void setup()
{
  Serial.begin(9600);
  //Inicializa o LCD
  lcd.begin(20, 4);
  Wire.begin();
  Wire.beginTransmission(MPU);
  Wire.write(0x6B); 
   
  //Inicializa o MPU-6050
  Wire.write(0); 
  Wire.endTransmission(true);
     
  //Informacoes iniciais do display
  lcd.setCursor(0,0);
  lcd.print("Acelerometro");
  lcd.setCursor(0,2);
  lcd.print("Giroscopio");
}
void loop()
{
  Wire.beginTransmission(MPU);
  Wire.write(0x3B);  // starting with register 0x3B (ACCEL_XOUT_H)
  Wire.endTransmission(false);
  //Solicita os dados do sensor
  Wire.requestFrom(MPU,14,true);  
  //Armazena o valor dos sensores nas variaveis correspondentes
  AcX=Wire.read()<<8|Wire.read();  //0x3B (ACCEL_XOUT_H) & 0x3C (ACCEL_XOUT_L)     
  AcY=Wire.read()<<8|Wire.read();  //0x3D (ACCEL_YOUT_H) & 0x3E (ACCEL_YOUT_L)
  AcZ=Wire.read()<<8|Wire.read();  //0x3F (ACCEL_ZOUT_H) & 0x40 (ACCEL_ZOUT_L)
  Tmp=Wire.read()<<8|Wire.read();  //0x41 (TEMP_OUT_H) & 0x42 (TEMP_OUT_L)
  GyX=Wire.read()<<8|Wire.read();  //0x43 (GYRO_XOUT_H) & 0x44 (GYRO_XOUT_L)
  GyY=Wire.read()<<8|Wire.read();  //0x45 (GYRO_YOUT_H) & 0x46 (GYRO_YOUT_L)
  GyZ=Wire.read()<<8|Wire.read();  //0x47 (GYRO_ZOUT_H) & 0x48 (GYRO_ZOUT_L)
   
  //Envia valor X do acelerometro para a serial e o LCD
  Serial.print("AcX = "); Serial.print(AcX);
  lcd.setCursor(0,1);
  lcd.print("X=");
  lcd.print(AcX);
   
  //Envia valor Y do acelerometro para a serial e o LCD
  Serial.print(" | AcY = "); Serial.print(AcY);
  lcd.setCursor(7,1);
  lcd.print("Y=");
  lcd.print(AcY);
   
  //Envia valor Z do acelerometro para a serial e o LCD
  Serial.print(" | AcZ = "); Serial.print(AcZ);
  lcd.setCursor(13,1);
  lcd.print("Z=");
  lcd.print(AcZ);
   
  //Envia valor da temperatura para a serial e o LCD
  //Calcula a temperatura em graus Celsius
  Serial.print(" | Tmp = "); Serial.print(Tmp/340.00+36.53);
  lcd.setCursor(13,0);
  lcd.print("T:");
  lcd.print(Tmp/340.00+36.53);
   
  //Envia valor X do giroscopio para a serial e o LCD
  Serial.print(" | GyX = "); Serial.print(GyX);
  lcd.setCursor(0,3);
  lcd.print("X=");
  lcd.print(GyX);
   
  //Envia valor Y do giroscopio para a serial e o LCD  
  Serial.print(" | GyY = "); Serial.print(GyY);
  lcd.setCursor(7,3);
  lcd.print("Y=");
  lcd.print(GyY);
   
  //Envia valor Z do giroscopio para a serial e o LCD
  Serial.print(" | GyZ = "); Serial.println(GyZ);
  lcd.setCursor(13,3);
  lcd.print("Z=");
  lcd.print(GyZ);
   
  //Aguarda 300 ms e reinicia o processo
  delay(300);
}

// code stored in the sketch: code_iDID.ino
//carrega biblioteca wire
#include<Wire.h>



String txt = "";
int AcX,AcY,AcZ,GyX,GyY,GyZ;
const int MPU=0x68;  


void setup(){
  Serial.begin(9600);
	//inicializa o acelerometro
  Wire.write(0); 
  Wire.endTransmission(true);
	
  
}

void loop(){
	Wire.beginTransmission(MPU);
  Wire.write(0x3B);  // starting with register 0x3B (ACCEL_XOUT_H)
  Wire.endTransmission(false);
	//solicita dados do sensor
  Wire.requestFrom(MPU,14,true);  
	//Armazena o valor dos sensores nas variaveis correspondentes
  AcX=Wire.read()<<8|Wire.read();  //0x3B (ACCEL_XOUT_H) & 0x3C (ACCEL_XOUT_L)     
  AcY=Wire.read()<<8|Wire.read();  //0x3D (ACCEL_YOUT_H) & 0x3E (ACCEL_YOUT_L)
  AcZ=Wire.read()<<8|Wire.read();  //0x3F (ACCEL_ZOUT_H) & 0x40 (ACCEL_ZOUT_L)
  GyX=Wire.read()<<8|Wire.read();  //0x43 (GYRO_XOUT_H) & 0x44 (GYRO_XOUT_L)
  GyY=Wire.read()<<8|Wire.read();  //0x45 (GYRO_YOUT_H) & 0x46 (GYRO_YOUT_L)
  GyZ=Wire.read()<<8|Wire.read();  //0x47 (GYRO_ZOUT_H) & 0x48 (GYRO_ZOUT_L)
  
	//traduzir valores do eixos para número
  

  //Aguarda 300 ms e reinicia o processo
  delay(300);
}

// code stored in the sketch: serialrxandfx.ino
//Programa : Modulo Bluetooth HC-06 - Leds
//Autor : Adilson Thomsen
 
//Armazena o caracter recebido
char buf;
 
void setup()
{
  //Define os pinos dos leds como saida
  pinMode(3, OUTPUT);
  pinMode(4, OUTPUT);
  pinMode(5, OUTPUT);
  Serial.begin(9600);
}
 
void loop()
{
  while(Serial.available() > 0)
  {
    buf = Serial.read();
    //Caso seja recebido R, acende o led vermelho
    if (buf == 'R')
    {
      digitalWrite(3, HIGH);
      Serial.println("LED Vermelho ligado !");
    }
    //Caso seja recebido G, acende o led verde
    if (buf == 'G')
    {
      digitalWrite(4, HIGH);
      Serial.println("LED Verde ligado !");
    }
    //Caso seja recebido B, acende o led azul
    if (buf == 'B')
    {
      digitalWrite(5, HIGH);
      Serial.println("LED Azul ligado !");
    }

  }
}

// code stored in the sketch: testeserial.ino
//Programa : Modulo bluetooth HC-06 - Configuracao
//Autor : Adilson Thomsen
 
//Carrega a biblioteca SoftwareSerial
#include <SoftwareSerial.h>
    
//Define os pinos para a serial  (RX, TX)
SoftwareSerial MinhaSerial(6,7);
String command = "";
    
void setup()  
{ 
  //Inicia a serial 
  Serial.begin(115200); 
  Serial.println("Digite os comandos AT :"); 
  //Inicia a serial configurada nas portas 6 e 7
  MinhaSerial.begin(9600); 
} 
    
void loop() 
{ 
  if (MinhaSerial.available())
  { 
     while(MinhaSerial.available())
     {
       command += (char)MinhaSerial.read(); 
     } 
   Serial.println(command); 
   command = ""; 
  } 
  
  if (Serial.available())
  { 
    delay(10);
    MinhaSerial.write(Serial.read()); 
  } 
}
